# Fritzing sketch scout_law_pico_power (saved by Fritzing 1.0.4)
# 18650 Li-ion Battery: CC-BY Dr Kristofer Chan, King's College London/Remote-research.org
breadboards: 1

parts:
  BAT1 = 18650 Li-ion Battery [package=battery-18650]
  Pico_H1 = Raspberry Pi Pico H
  Pico_Lipo_SHIM1 = Pimoroni Pico Lipo SHIM [package="DIP (Dual Inline) [THT]"]

nets:
  N1: BAT1.-, Pico_Lipo_SHIM1.pin_18
  N2: BAT1.+, Pico_Lipo_SHIM1.pin_17
  N3: Pico_H1.VBUS, Pico_Lipo_SHIM1.pin1
  N4: Pico_H1.VSYS, Pico_Lipo_SHIM1.pin2
  N5: Pico_H1.GND, Pico_Lipo_SHIM1.pin3, Pico_Lipo_SHIM1.pin11
  N6: Pico_H1.3V3_EN, Pico_Lipo_SHIM1.pin4
  N7: Pico_H1.3V3, Pico_Lipo_SHIM1.pin5
  N8: Pico_H1.ADC_VREF, Pico_Lipo_SHIM1.pin6
  N9: Pico_H1.GP28_A2, Pico_Lipo_SHIM1.pin7
  N10: Pico_H1.GP4, Pico_Lipo_SHIM1.pin14
  N11: Pico_H1.GP3, Pico_Lipo_SHIM1.pin13
  N12: Pico_H1.GP2, Pico_Lipo_SHIM1.pin12
  N13: Pico_H1.GP1, Pico_Lipo_SHIM1.pin10
  N14: Pico_H1.GP0, Pico_Lipo_SHIM1.pin9

custom parts:
  18650 Li-ion Battery: 18650 li-ion Battery Standard 18650 battery with interactive connectors Creative Common Attribution 4.0 International (CC-BY 4.0) license. Any use of this part requires attribution of Dr Kristofer Chan, Department of Geography, King's College London. Contact kristofer.chan [at] kcl.ac.uk OR kris [at] remote-research.org for further information.
  Raspberry Pi Pico H: Raspberry Pi Pico H. Based around the RP2040 microcontroller the Pico H is a low cost microcontroller device bringing Raspberry Pi quality, cost, and easy of use to the microcontroller space.
  Pimoroni Pico Lipo SHIM: The Pico Lipo SHIM by Pimoroni
